# Fritzing sketch beacon_diagram (saved by Fritzing 0.9.4)
breadboards: 2

parts:
  ESP32_-_Back1 = ESP32 - CAM
  U1 = GPS6MV2 [package=GSP6MV2]
  GY1 = MPU-6050 Board GY-521 [form="♀ (female)" package=THT]
  M1 = BMP280
  LED3 = smd LED [color="White (6500K)" package="1206 [SMD]"]
  BAT2 = Battery Holders [package=lipo-1100mAh]  # not connected
  Argon1 = Particle Argon

nets:
  GND: ESP32_-_Back1.GND#7, U1.GND, GY1.pin2, M1.GND, LED3.cathode, Argon1.GND
  3.3V: ESP32_-_Back1.3.3V, U1.VCC, GY1.pin1, M1.VIN, Argon1.3.3V
  N1: U1.TX-O, Argon1.TX
  N2: U1.RX-I, Argon1.RX
  N3: GY1.pin3, M1.SCL, Argon1.SCL
  N4: GY1.pin4, M1.SDA, Argon1.SDA
  N5: LED3.anode, Argon1.MI

custom parts:
  ESP32 - CAM: The ESP32-CAM has a very competitive small-size camera module that can operate independently as a minimum system with a footprint of only 27*40.5*4.5mm and a deep sleep current of up to 6mA.
  GPS6MV2: GPS transciever
  MPU-6050 Board GY-521: Acelerometro y Giroscopio MPU-6050 Board GY-521
  BMP280: Temperature Humidity Barometric presure Sensor, I2C
  Particle Argon: The Argon is a powerful Wi-Fi enabled development board that can act as either a standalone Wi-Fi endpoint or Wi-Fi enabled gateway for Particle Mesh networks. It is based on the Nordic nRF52840 and has built-in battery charging circuitry so it’s easy to connect a Li-Po and deploy your local network in minutes. The Argon is great for connecting existing projects to the Particle Device Cloud or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
